# Fritzing sketch pln2033 (saved by Fritzing 0.9.0b)

parts:
  BeagleBone1 = BeagleBone Black
  S1 = Generic shrouded header - 10 pins [form="♂ (shrouded male)" package=THT]
  S2 = Generic shrouded header - 10 pins [form="♂ (shrouded male)" package=THT]

nets:
  N1: BeagleBone1.no_name_yet#1, S1.pin6
  N2: BeagleBone1.no_name_yet#5, S1.pin5
  N3: BeagleBone1.no_name_yet#28, S1.pin2
  N4: BeagleBone1.no_name_yet#29, S2.pin9
  N5: BeagleBone1.no_name_yet#30, S2.pin10
  N6: BeagleBone1.no_name_yet#31, S2.pin1
  N7: BeagleBone1.no_name_yet#42, S2.pin2

notes:
  GND
  VCC
  SPI1_CS0
  SPI1_CS1
  MISO
  MOSI
  CLK

custom parts:
  BeagleBone Black: BeagleBone Black rev. A5B
  Generic shrouded header - 10 pins: Generic shrouded header
